// Logisim project AU.circ as structural Verilog: 1 circuit, main circuit main
module main (
  input  in_1,
  input  [7:0] in_2,
  input  [7:0] in_3,
  input  [1:0] in_4,
  output [7:0] out_5,
  output out_6
);

  wire [7:0] multiplexer_1_out, not_1_out;

  assign not_1_out = ~in_3;  // NOT_Gate not_1, 8 bits wide
  Multiplexer #(.select(2), .width(8)) multiplexer_1 (
    .in0(in_3), .in1(not_1_out), .in2({8{1'b0}}), .in3({8{1'b1}}), .out(multiplexer_1_out), .sel(in_4));
  Adder adder_1 (.a(in_2), .b(multiplexer_1_out), .out(out_5), .cin(in_1), .cout(out_6));
endmodule
